# Fritzing sketch esquematico (saved by Fritzing 0.8.5b)
breadboards: 1

parts:
  J1 = Screw terminal - 2 pins [package=THT]
  J2 = Screw terminal - 2 pins [package=THT]
  J3 = Screw terminal - 2 pins [package=THT]
  J4 = Screw terminal - 2 pins [package=THT]
  J5 = Screw terminal - 2 pins [package=THT]
  IC2 = L293D [package=THT]
  VCC1 = Battery block 9V
  M1 = DC Motor
  M2 = DC Motor
  Parte1 = Arduino Uno (Rev3)
  M3 = Stepper Motor - Bipolar
  Part2 = Bluetooth HC-05 Macho

nets:
  N1: J1.pin1, IC2.0V
  N2: J1.pin2, IC2.Enable_1, IC2.+Vmotor, IC2.Enable_2, IC2.+V, VCC1.+
  N3: J2.pin1, IC2.In_3, Parte1.D12/MISO
  N4: J2.pin2, IC2.In_4, Parte1.D11_PWM/MOSI
  N5: J3.pin1, IC2.In_1, Parte1.D10_PWM/SS
  N6: J3.pin2, IC2.In_2, Parte1.D9_PWM
  N7: J4.pin1, IC2.Out_1_(_Controlled_by_Enable_1_), M2.pin_2, M3.B
  N8: J4.pin2, IC2.Out_2_(_Controlled_by_Enable_1_), M2.pin_1, M3.D
  N9: J5.pin1, IC2.Out_3_(_Controlled_by_Enable_2_), M1.pin_1, M3.C
  N10: J5.pin2, IC2.Out_4_(_Controlled_by_Enable_2_), M1.pin_2, M3.A
  GND: Parte1.GND, Part2.GND
  N11: Parte1.D0/RX, Part2.TXD
  N12: Parte1.D1/TX, Part2.RXD

notes:
  5v
